// Digital circuit 10X15 SRAM.dig as structural Verilog
module _10X15_SRAM (
  input  [3:0] WR_3_0,
  input  CLK,
  input  [14:0] WRD_14_0,
  input  [3:0] RA1_3_0,
  input  [3:0] RA2_3_0,
  input  WE,
  output [14:0] RD1_14_0,
  output [14:0] RD2_14_0
);

  wire decoder_1_out_10, decoder_1_out_11, decoder_1_out_12, decoder_1_out_13, decoder_1_out_14,
       decoder_1_out_15, decoder_2_out_10, decoder_2_out_11, decoder_2_out_12, decoder_2_out_13,
       decoder_2_out_14, decoder_2_out_15, decoder_3_out_10, decoder_3_out_11, decoder_3_out_12,
       decoder_3_out_13, decoder_3_out_14, decoder_3_out_15, R1_0, R1_1, R1_2, R1_3, R1_4, R1_5, R1_6, R1_7,
       R1_8, R1_9, R2_0, R2_1, R2_2, R2_3, R2_4, R2_5, R2_6, R2_7, R2_8, R2_9, W0, W1, W2, W3, W4, W5, W6,
       W7, W8, W9, WS0, WS1, WS2, WS3, WS4, WS5, WS6, WS7, WS8, WS9;
  wire [14:0] or_1_out, or_2_out, or_3_out, or_4_out, RD1_0, RD1_1, RD1_2, RD1_3, RD1_4, RD1_5, RD1_6, RD1_7,
       RD1_8, RD1_9, RD2_0, RD2_1, RD2_2, RD2_3, RD2_4, RD2_5, RD2_6, RD2_7, RD2_8, RD2_9;

  and and_1 (WS8, WE, W8);
  and and_2 (WS6, WE, W6);
  and and_3 (WS0, WE, W0);
  and and_4 (WS1, WE, W1);
  and and_5 (WS4, WE, W4);
  and and_6 (WS7, WE, W7);
  and and_7 (WS2, WE, W2);
  and and_8 (WS9, WE, W9);
  and and_9 (WS3, WE, W3);
  and and_10 (WS5, WE, W5);
  Decoder #(.Selector_Bits(4)) decoder_1 (
    .sel(RA1_3_0), .out_0(R1_0), .out_1(R1_1), .out_2(R1_2), .out_3(R1_3), .out_4(R1_4), .out_5(R1_5),
    .out_6(R1_6), .out_7(R1_7), .out_8(R1_8), .out_9(R1_9), .out_10(decoder_1_out_10),
    .out_11(decoder_1_out_11), .out_12(decoder_1_out_12), .out_13(decoder_1_out_13),
    .out_14(decoder_1_out_14), .out_15(decoder_1_out_15));
  Decoder #(.Selector_Bits(4)) decoder_2 (
    .sel(WR_3_0), .out_0(W0), .out_1(W1), .out_2(W2), .out_3(W3), .out_4(W4), .out_5(W5), .out_6(W6),
    .out_7(W7), .out_8(W8), .out_9(W9), .out_10(decoder_2_out_10), .out_11(decoder_2_out_11),
    .out_12(decoder_2_out_12), .out_13(decoder_2_out_13), .out_14(decoder_2_out_14), .out_15(decoder_2_out_15));
  Decoder #(.Selector_Bits(4)) decoder_3 (
    .sel(RA2_3_0), .out_0(R2_0), .out_1(R2_1), .out_2(R2_2), .out_3(R2_3), .out_4(R2_4), .out_5(R2_5),
    .out_6(R2_6), .out_7(R2_7), .out_8(R2_8), .out_9(R2_9), .out_10(decoder_3_out_10),
    .out_11(decoder_3_out_11), .out_12(decoder_3_out_12), .out_13(decoder_3_out_13),
    .out_14(decoder_3_out_14), .out_15(decoder_3_out_15));
  _1x15_SRAM _1x15_sram_1 (
    .RS1(R1_9), .RS2(R2_9), .WS(WS9), .WD_14_0(WRD_14_0), .CLK(CLK), .RD1_14_0(RD1_9), .RD2_14_0(RD2_9));
  _1x15_SRAM _1x15_sram_2 (
    .RS1(R1_8), .RS2(R2_8), .WS(WS8), .WD_14_0(WRD_14_0), .CLK(CLK), .RD1_14_0(RD1_8), .RD2_14_0(RD2_8));
  _1x15_SRAM _1x15_sram_3 (
    .RS1(R1_7), .RS2(R2_7), .WS(WS7), .WD_14_0(WRD_14_0), .CLK(CLK), .RD1_14_0(RD1_7), .RD2_14_0(RD2_7));
  _1x15_SRAM _1x15_sram_4 (
    .RS1(R1_6), .RS2(R2_6), .WS(WS6), .WD_14_0(WRD_14_0), .CLK(CLK), .RD1_14_0(RD1_6), .RD2_14_0(RD2_6));
  _1x15_SRAM _1x15_sram_5 (
    .RS1(R1_5), .RS2(R2_5), .WS(WS5), .WD_14_0(WRD_14_0), .CLK(CLK), .RD1_14_0(RD1_5), .RD2_14_0(RD2_5));
  _1x15_SRAM _1x15_sram_6 (
    .RS1(R1_4), .RS2(R2_4), .WS(WS4), .WD_14_0(WRD_14_0), .CLK(CLK), .RD1_14_0(RD1_4), .RD2_14_0(RD2_4));
  _1x15_SRAM _1x15_sram_7 (
    .RS1(R1_3), .RS2(R2_3), .WS(WS3), .WD_14_0(WRD_14_0), .CLK(CLK), .RD1_14_0(RD1_3), .RD2_14_0(RD2_3));
  _1x15_SRAM _1x15_sram_8 (
    .RS1(R1_2), .RS2(R2_2), .WS(WS2), .WD_14_0(WRD_14_0), .CLK(CLK), .RD1_14_0(RD1_2), .RD2_14_0(RD2_2));
  _1x15_SRAM _1x15_sram_9 (
    .RS1(R1_1), .RS2(R2_1), .WS(WS1), .WD_14_0(WRD_14_0), .CLK(CLK), .RD1_14_0(RD1_1), .RD2_14_0(RD2_1));
  _1x15_SRAM _1x15_sram_10 (
    .RS1(R1_0), .RS2(R2_0), .WS(WS0), .WD_14_0(WRD_14_0), .CLK(CLK), .RD1_14_0(RD1_0), .RD2_14_0(RD2_0));
  assign or_1_out = RD1_0 | RD1_1 | RD1_2 | RD1_3 | RD1_4;  // Or or_1, 15 bits wide
  assign or_2_out = RD1_5 | RD1_6 | RD1_7 | RD1_8 | RD1_9;  // Or or_2, 15 bits wide
  assign or_3_out = RD2_0 | RD2_1 | RD2_2 | RD2_3 | RD2_4;  // Or or_3, 15 bits wide
  assign or_4_out = RD2_5 | RD2_6 | RD2_7 | RD2_8 | RD2_9;  // Or or_4, 15 bits wide
  assign RD1_14_0 = or_1_out | or_2_out;  // Or or_5, 15 bits wide
  assign RD2_14_0 = or_3_out | or_4_out;  // Or or_6, 15 bits wide
  // also tied to GND on the sheet: {decoder_3_out_10, decoder_3_out_11, decoder_3_out_12, decoder_3_out_13, decoder_3_out_14, decoder_3_out_15, decoder_2_out_10, decoder_2_out_11, decoder_2_out_12, decoder_2_out_13, decoder_2_out_14, decoder_2_out_15, decoder_1_out_10, decoder_1_out_11, decoder_1_out_12, decoder_1_out_13, decoder_1_out_14, decoder_1_out_15}

  // Other names for the same wires on the sheet: WRD[14:0] = WRD_14_0
endmodule
