// Digital circuit 4bit PC Reg.dig as structural Verilog
module _4bit_PC_Reg (
  input  [3:0] I_3_0,
  input  CLK,
  output [3:0] O_3_0
);

  _1_bit_Reg _1_bit_reg_1 (.Dout(O_3_0[3]), .Din(I_3_0[3]), .Sel(1'b1), .CLK(CLK));
  _1_bit_Reg _1_bit_reg_2 (.Dout(O_3_0[2]), .Din(I_3_0[2]), .Sel(1'b1), .CLK(CLK));
  _1_bit_Reg _1_bit_reg_3 (.Dout(O_3_0[1]), .Din(I_3_0[1]), .Sel(1'b1), .CLK(CLK));
  _1_bit_Reg _1_bit_reg_4 (.Dout(O_3_0[0]), .Din(I_3_0[0]), .Sel(1'b1), .CLK(CLK));

  // Other names for the same wires on the sheet: B0 = O_3_0[0]; B1 = O_3_0[1]; B2 = O_3_0[2]; B3 = O_3_0[3];
  //   A0 = I_3_0[0]; A1 = I_3_0[1]; A2 = I_3_0[2]; A3 = I_3_0[3]
endmodule
