// Digital circuit 4bit_CU.dig as structural Verilog
module _4bit_CU (
  input  [3:0] OpCode_3_0,
  input  ZF,
  output [1:0] Op_1_0,
  output REG_EN,
  output Imm_sel,
  output Jmp_sel
);

  wire and_1_out, and_3_out, and_4_out, and_5_out, or_2_out;

  and and_1 (and_1_out, ~OpCode_3_0[2], ~OpCode_3_0[3]);  // And
  and and_2 (Imm_sel, OpCode_3_0[2], ~OpCode_3_0[3]);  // And
  and and_3 (and_3_out, ~OpCode_3_0[2], OpCode_3_0[3]);  // And
  and and_4 (and_4_out, ~OpCode_3_0[0], ~OpCode_3_0[1]);  // And
  and and_5 (and_5_out, OpCode_3_0[0], ~OpCode_3_0[1], ~ZF);  // And
  or or_1 (REG_EN, and_1_out, Imm_sel);
  or or_2 (or_2_out, and_4_out, and_5_out);
  and and_6 (Jmp_sel, and_3_out, or_2_out);

  assign Op_1_0 = OpCode_3_0[1:0];
endmodule
