// Digital circuit 5-Bit ALU.dig as structural Verilog
module _5_Bit_ALU (
  input  [4:0] A_4_0,
  input  [4:0] B_4_0,
  input  [1:0] Op_1_0,
  output [4:0] R_4_0
);

  wire [4:0] _5_bit_adder_1_r_4_0, _5_bit_or_1_r_4_0, _5_bit_ror_1_r_4_0;

  _5_bit_Adder _5_bit_adder_1 (.A_4_0(A_4_0), .B_4_0(B_4_0), .R_4_0(_5_bit_adder_1_r_4_0));  // open: Cout
  _5_bit_ROR _5_bit_ror_1 (.R_4_0(_5_bit_ror_1_r_4_0), .A_4_0(A_4_0), .B_4_0(B_4_0));
  _5_bit_OR _5_bit_or_1 (.A_4_0(A_4_0), .B_4_0(B_4_0), .R_4_0(_5_bit_or_1_r_4_0));
  Multiplexer #(.Selector_Bits(2), .Bits(5)) multiplexer_1 (
    .sel(Op_1_0), .in_0(_5_bit_adder_1_r_4_0), .in_1(_5_bit_ror_1_r_4_0), .in_2(_5_bit_or_1_r_4_0),
    .in_3({5{1'b0}}), .out(R_4_0));
endmodule
