// Digital circuit 5-bit Adder.dig as structural Verilog
module _5_bit_Adder (
  input  [4:0] A_4_0,
  input  [4:0] B_4_0,
  output Cout,
  output [4:0] R_4_0
);

  wire fa_2_cout, fa_3_cout, fa_4_cout, fa_5_cout;

  FA fa_1 (.A(A_4_0[4]), .B(B_4_0[4]), .Cin(fa_2_cout), .S(R_4_0[4]), .Cout(Cout));
  FA fa_2 (.A(A_4_0[3]), .B(B_4_0[3]), .Cin(fa_3_cout), .S(R_4_0[3]), .Cout(fa_2_cout));
  FA fa_3 (.A(A_4_0[2]), .B(B_4_0[2]), .Cin(fa_4_cout), .S(R_4_0[2]), .Cout(fa_3_cout));
  FA fa_4 (.A(A_4_0[1]), .B(B_4_0[1]), .Cin(fa_5_cout), .S(R_4_0[1]), .Cout(fa_4_cout));
  FA fa_5 (.A(A_4_0[0]), .B(B_4_0[0]), .Cin(1'b0), .S(R_4_0[0]), .Cout(fa_5_cout));
endmodule
