// Digital circuit 5-bit ROR.dig as structural Verilog
module _5_bit_ROR (
  input  [4:0] A_4_0,
  input  [4:0] B_4_0,
  output [4:0] R_4_0
);

  Multiplexer #(.Selector_Bits(5)) multiplexer_1 (
    .sel(B_4_0), .in_0(A_4_0[4]), .in_1(A_4_0[0]), .in_2(A_4_0[1]), .in_3(A_4_0[2]), .in_4(A_4_0[3]),
    .in_5(A_4_0[4]), .in_6(1'b0), .in_7(1'b0), .in_8(1'b0), .in_9(1'b0), .in_10(1'b0), .in_11(1'b0),
    .in_12(1'b0), .in_13(1'b0), .in_14(1'b0), .in_15(1'b0), .in_16(1'b0), .in_17(1'b0), .in_18(1'b0),
    .in_19(1'b0), .in_20(1'b0), .in_21(1'b0), .in_22(1'b0), .in_23(1'b0), .in_24(1'b0), .in_25(1'b0),
    .in_26(1'b0), .in_27(1'b0), .in_28(1'b0), .in_29(1'b0), .in_30(1'b0), .in_31(1'b0), .out(R_4_0[4]));
  Multiplexer #(.Selector_Bits(5)) multiplexer_2 (
    .sel(B_4_0), .in_0(A_4_0[3]), .in_1(A_4_0[4]), .in_2(A_4_0[0]), .in_3(A_4_0[1]), .in_4(A_4_0[2]),
    .in_5(A_4_0[3]), .in_6(1'b0), .in_7(1'b0), .in_8(1'b0), .in_9(1'b0), .in_10(1'b0), .in_11(1'b0),
    .in_12(1'b0), .in_13(1'b0), .in_14(1'b0), .in_15(1'b0), .in_16(1'b0), .in_17(1'b0), .in_18(1'b0),
    .in_19(1'b0), .in_20(1'b0), .in_21(1'b0), .in_22(1'b0), .in_23(1'b0), .in_24(1'b0), .in_25(1'b0),
    .in_26(1'b0), .in_27(1'b0), .in_28(1'b0), .in_29(1'b0), .in_30(1'b0), .in_31(1'b0), .out(R_4_0[3]));
  Multiplexer #(.Selector_Bits(5)) multiplexer_3 (
    .sel(B_4_0), .in_0(A_4_0[2]), .in_1(A_4_0[3]), .in_2(A_4_0[4]), .in_3(A_4_0[0]), .in_4(A_4_0[1]),
    .in_5(A_4_0[2]), .in_6(1'b0), .in_7(1'b0), .in_8(1'b0), .in_9(1'b0), .in_10(1'b0), .in_11(1'b0),
    .in_12(1'b0), .in_13(1'b0), .in_14(1'b0), .in_15(1'b0), .in_16(1'b0), .in_17(1'b0), .in_18(1'b0),
    .in_19(1'b0), .in_20(1'b0), .in_21(1'b0), .in_22(1'b0), .in_23(1'b0), .in_24(1'b0), .in_25(1'b0),
    .in_26(1'b0), .in_27(1'b0), .in_28(1'b0), .in_29(1'b0), .in_30(1'b0), .in_31(1'b0), .out(R_4_0[2]));
  Multiplexer #(.Selector_Bits(5)) multiplexer_4 (
    .sel(B_4_0), .in_0(A_4_0[1]), .in_1(A_4_0[2]), .in_2(A_4_0[3]), .in_3(A_4_0[4]), .in_4(A_4_0[0]),
    .in_5(A_4_0[1]), .in_6(1'b0), .in_7(1'b0), .in_8(1'b0), .in_9(1'b0), .in_10(1'b0), .in_11(1'b0),
    .in_12(1'b0), .in_13(1'b0), .in_14(1'b0), .in_15(1'b0), .in_16(1'b0), .in_17(1'b0), .in_18(1'b0),
    .in_19(1'b0), .in_20(1'b0), .in_21(1'b0), .in_22(1'b0), .in_23(1'b0), .in_24(1'b0), .in_25(1'b0),
    .in_26(1'b0), .in_27(1'b0), .in_28(1'b0), .in_29(1'b0), .in_30(1'b0), .in_31(1'b0), .out(R_4_0[1]));
  Multiplexer #(.Selector_Bits(5)) multiplexer_5 (
    .sel(B_4_0), .in_0(A_4_0[0]), .in_1(A_4_0[1]), .in_2(A_4_0[2]), .in_3(A_4_0[3]), .in_4(A_4_0[4]),
    .in_5(A_4_0[0]), .in_6(1'b0), .in_7(1'b0), .in_8(1'b0), .in_9(1'b0), .in_10(1'b0), .in_11(1'b0),
    .in_12(1'b0), .in_13(1'b0), .in_14(1'b0), .in_15(1'b0), .in_16(1'b0), .in_17(1'b0), .in_18(1'b0),
    .in_19(1'b0), .in_20(1'b0), .in_21(1'b0), .in_22(1'b0), .in_23(1'b0), .in_24(1'b0), .in_25(1'b0),
    .in_26(1'b0), .in_27(1'b0), .in_28(1'b0), .in_29(1'b0), .in_30(1'b0), .in_31(1'b0), .out(R_4_0[0]));

  // Other names for the same wires on the sheet: A0 = A_4_0[0]; A1 = A_4_0[1]; A2 = A_4_0[2]; A3 = A_4_0[3];
  //   A4 = A_4_0[4]; Sel[4:0] = B_4_0
endmodule
