// Digital circuit 5-bit Reg.dig as structural Verilog
module _5_bit_Reg (
  input  [4:0] Din_4_0,
  input  Sel,
  input  CLK,
  output [4:0] Dout_4_0
);

  _1_bit_Reg _1_bit_reg_1 (.Dout(Dout_4_0[4]), .Din(Din_4_0[4]), .Sel(Sel), .CLK(CLK));
  _1_bit_Reg _1_bit_reg_2 (.Dout(Dout_4_0[3]), .Din(Din_4_0[3]), .Sel(Sel), .CLK(CLK));
  _1_bit_Reg _1_bit_reg_3 (.Dout(Dout_4_0[2]), .Din(Din_4_0[2]), .Sel(Sel), .CLK(CLK));
  _1_bit_Reg _1_bit_reg_4 (.Dout(Dout_4_0[1]), .Din(Din_4_0[1]), .Sel(Sel), .CLK(CLK));
  _1_bit_Reg _1_bit_reg_5 (.Dout(Dout_4_0[0]), .Din(Din_4_0[0]), .Sel(Sel), .CLK(CLK));

  // Other names for the same wires on the sheet: B0 = Dout_4_0[0]; B1 = Dout_4_0[1]; B2 = Dout_4_0[2];
  //   B3 = Dout_4_0[3]; B4 = Dout_4_0[4]; A0 = Din_4_0[0]; A1 = Din_4_0[1]; A2 = Din_4_0[2]; A3 = Din_4_0[3];
  //   A4 = Din_4_0[4]
endmodule
