// Digital circuit 5-bit3reg-reg set.dig as structural Verilog
module _5_bit3reg_reg_set (
  input  [1:0] RA_1_0,
  input  [1:0] RB_1_0,
  input  [1:0] WR_1_0,
  input  [4:0] WRD_4_0,
  input  WE,
  input  CLK,
  output [4:0] A_4_0,
  output [4:0] B_4_0
);

  wire A0, A1, A2, D0, D1, D2, decoder_1_out_3;
  wire [4:0] R0, R1, R2;

  and and_1 (D2, WE, A2);
  and and_2 (D1, WE, A1);
  Decoder #(.Selector_Bits(2)) decoder_1 (.sel(WR_1_0), .out_0(A0), .out_1(A1), .out_2(A2), .out_3(decoder_1_out_3));
  and and_3 (D0, WE, A0);
  _5_bit_Reg _5_bit_reg_1 (.Din_4_0(WRD_4_0), .Sel(D2), .CLK(CLK), .Dout_4_0(R2));
  _5_bit_Reg _5_bit_reg_2 (.Din_4_0(WRD_4_0), .Sel(D1), .CLK(CLK), .Dout_4_0(R1));
  _5_bit_Reg _5_bit_reg_3 (.Din_4_0(WRD_4_0), .Sel(D0), .CLK(CLK), .Dout_4_0(R0));
  Multiplexer #(.Selector_Bits(2), .Bits(5)) multiplexer_1 (
    .sel(RA_1_0), .in_0(R0), .in_1(R1), .in_2(R2), .in_3({5{1'b0}}), .out(A_4_0));
  Multiplexer #(.Selector_Bits(2), .Bits(5)) multiplexer_2 (
    .sel(RB_1_0), .in_0(R0), .in_1(R1), .in_2(R2), .in_3({5{1'b0}}), .out(B_4_0));
  // also tied to GND on the sheet: decoder_1_out_3

  // Other names for the same wires on the sheet: Din[4:0] = WRD_4_0
endmodule
