// Digital circuit CPU.dig as structural Verilog
module CPU (
  input  [3:0] WR_3_0,
  input  [14:0] WRD_14_0,
  input  WE,
  input  CLK,
  input  PC_EN,
  input  [3:0] RA2_3_0,
  input  ZF,
  output [14:0] RD2_14_0,
  output [1:0] R1_1_0,
  output [1:0] R2_1_0,
  output [1:0] WR_1_0,
  output [4:0] R_4_0,
  output [4:0] A_4_0,
  output [4:0] B_4_0,
  output [3:0] JMP_ADD
);

  wire CPU_CLK, Imm_sel, Jmp_sel, REG_EN;
  wire [1:0] Op;
  wire [3:0] _4bit_pc_adder_1_o_3_0, _4bit_pc_reg_1_o_3_0, multiplexer_1_out, OpCode;
  wire [4:0] _5_bit3reg_reg_set_1_b_4_0;
  wire [6:0] dont_care;

  Multiplexer #(.Bits(4)) multiplexer_1 (
    .sel(Jmp_sel), .in_0(_4bit_pc_adder_1_o_3_0), .in_1(JMP_ADD), .out(multiplexer_1_out));
  _4bit_PC_adder _4bit_pc_adder_1 (.I_3_0(_4bit_pc_reg_1_o_3_0), .O_3_0(_4bit_pc_adder_1_o_3_0));
  _4bit_PC_Reg _4bit_pc_reg_1 (.I_3_0(multiplexer_1_out), .CLK(CPU_CLK), .O_3_0(_4bit_pc_reg_1_o_3_0));
  and and_1 (CPU_CLK, PC_EN, CLK);
  _10X15_SRAM _10x15_sram_1 (
    .RA1_3_0(_4bit_pc_reg_1_o_3_0), .RA2_3_0(RA2_3_0), .WR_3_0(WR_3_0), .WRD_14_0(WRD_14_0), .WE(WE),
    .CLK(CLK), .RD1_14_0({OpCode, JMP_ADD, dont_care}), .RD2_14_0(RD2_14_0));
  _4bit_CU _4bit_cu_1 (
    .OpCode_3_0(OpCode), .ZF(ZF), .Op_1_0(Op), .REG_EN(REG_EN), .Imm_sel(Imm_sel), .Jmp_sel(Jmp_sel));
  _5_bit3reg_reg_set _5_bit3reg_reg_set_1 (
    .RA_1_0(JMP_ADD[3:2]), .RB_1_0(JMP_ADD[1:0]), .WR_1_0(JMP_ADD[3:2]), .CLK(CPU_CLK), .WE(REG_EN),
    .WRD_4_0(R_4_0), .A_4_0(A_4_0), .B_4_0(_5_bit3reg_reg_set_1_b_4_0));
  _5_Bit_ALU _5_bit_alu_1 (.R_4_0(R_4_0), .A_4_0(A_4_0), .B_4_0(B_4_0), .Op_1_0(Op));
  Multiplexer #(.Bits(5)) multiplexer_2 (
    .sel(Imm_sel), .in_0(_5_bit3reg_reg_set_1_b_4_0), .in_1({JMP_ADD[1:0], dont_care[6:4]}), .out(B_4_0));

  assign R1_1_0 = JMP_ADD[3:2];
  assign R2_1_0 = JMP_ADD[1:0];
  assign WR_1_0 = JMP_ADD[3:2];

  // Other names for the same wires on the sheet: xx[3:0] = dont_care[3:0];
  //   Im_Value[4:0] = {JMP_ADD[1:0], dont_care[6:4]}; R2[1:0] = JMP_ADD[1:0]; R1[1:0] = JMP_ADD[3:2]; A[4:0] = A_4_0;
  //   B[4:0] = B_4_0; R[4:0] = R_4_0; RA2[3:0] = RA2_3_0; RD2[14:0] = RD2_14_0; WR[3:0] = WR_3_0;
  //   WRD[14:0] = WRD_14_0

  // Notes on the sheet:
  //   Register Mode(type Of Op==00)2bit(Type of op)+2bit(op)+2bit(Reg1)+ 2bit(Reg2)+7 bit don’t care
  //   Imm  Mode(type Of Op==01)2bit(Type of op)+2bit(op)+2bit(Reg 1)+ 5bit(Imm value)+4bit don’t care
  //   Jump Mode(type Of Op==10)2bit(Type of op)+2bit(op)+4bit(Addr)+ 7bit don’t care
  //   Add(op=00),ROR(op=01),OR(op=10)
  //   JMP(Op=00),JNE(Op=01)
  //   JNE START ->100100010000000
  //   START: OR R1, R1  ->001001010000000
  //   JMPTO:ADD R1,5 ->010001001010000
  //   JMP JMPTO -> 100000010000000
endmodule
